// Logisim project CRC.circ as structural Verilog: 3 circuits, main circuit main
module main (
  input  [3:0] in_1,
  input  [3:0] in_2,
  output [3:0] out_3
);

  wire and_1_out;
  wire [3:0] multiplexer_1_out;

  Multiplexer #(.width(4)) multiplexer_1 (
    .in0(4'b0000), .in1(in_2), .out(multiplexer_1_out), .sel(and_1_out));  // open: en
  assign out_3 = in_1 ^ multiplexer_1_out;  // XOR_Gate xor_1, 4 bits wide
  and and_1 (and_1_out, in_1[3], in_2[3]);
endmodule

module module2 (
  input  [7:0] in_1,
  input  [3:0] in_2,
  output [10:0] out_3
);

  wire [3:0] s1, s2, s3, s4, s5, s6, s7;
  wire [3:3] s8;

  main main_1 (.in_1(in_1[7:4]), .in_2(in_2), .out_3(s1));
  main main_2 (.in_1({s1[2:0], in_1[3]}), .in_2(in_2), .out_3(s2));
  main main_3 (.in_1({s2[2:0], in_1[2]}), .in_2(in_2), .out_3(s3));
  main main_4 (.in_1({s3[2:0], in_1[1]}), .in_2(in_2), .out_3(s4));
  main main_5 (.in_1({s4[2:0], in_1[0]}), .in_2(in_2), .out_3(s5));
  main main_6 (.in_1({s5[2:0], 1'b0}), .in_2(in_2), .out_3(s6));
  main main_7 (.in_1({s6[2:0], 1'b0}), .in_2(in_2), .out_3(s7));
  main main_8 (.in_1({s7[2:0], 1'b0}), .in_2(in_2), .out_3({s8[3], out_3[2:0]}));

  assign out_3[10:3] = in_1;

  // Other names for the same wires on the sheet: divider[3:0] = in_2; s8[2:0] = out_3[2:0]; div[7:0] = in_1;
  //   out5 = in_1[0]; sout4[3:0] = {s4[2:0], in_1[0]}; out4 = in_1[1]; sout3[3:0] = {s3[2:0], in_1[1]};
  //   out3 = in_1[2]; sout2[3:0] = {s2[2:0], in_1[2]}; out2 = in_1[3]; sout1[3:0] = {s1[2:0], in_1[3]};
  //   out1[3:0] = in_1[7:4]; sout5[3:1] = s5[2:0]; sout6[3:1] = s6[2:0]; sout7[3:1] = s7[2:0]
endmodule

module CRC (
  input  [7:0] in_1,
  input  [3:0] in_2,
  output [10:0] out_3
);

  module2 module2_1 (.in_1(in_1), .in_2(in_2), .out_3(out_3));
endmodule
