// Logisim project fsm.circ as structural Verilog: 4 circuits, main circuit 输出函数
module \输出函数  (
  input  in2,
  input  statex,
  input  statey,
  output out
);

  wire not_1_out, not_2_out;

  and and_1 (out, statex, not_1_out, not_2_out);
  not not_1 (not_1_out, statey);
  not not_2 (not_2_out, in2);
endmodule

module \次态逻辑  (
  input  statex,
  input  statey,
  input  in1,
  input  in2,
  input  clr,
  output statex2,
  output statey2
);

  wire and_1_out, and_2_out, and_3_out, and_4_out, and_5_out, not_1_out, not_2_out, not_3_out, not_4_out,
       not_5_out, not_6_out, not_7_out, not_8_out, not_9_out, not_10_out, not_11_out, not_12_out, not_13_out;

  not not_1 (not_1_out, statex);
  not not_2 (not_2_out, in2);
  not not_3 (not_3_out, clr);
  not not_4 (not_4_out, statex);
  not not_5 (not_5_out, in2);
  not not_6 (not_6_out, statey);
  not not_7 (not_7_out, in2);
  not not_8 (not_8_out, clr);
  not not_9 (not_9_out, in1);
  not not_10 (not_10_out, clr);
  not not_11 (not_11_out, statey);
  not not_12 (not_12_out, in2);
  not not_13 (not_13_out, clr);
  and and_1 (and_1_out, not_1_out, statey, not_2_out, not_3_out);
  and and_2 (and_2_out, not_4_out, statey, in1, not_5_out);
  and and_3 (and_3_out, statex, not_6_out, not_7_out, not_8_out);
  and and_4 (and_4_out, not_9_out, in2, not_10_out);
  and and_5 (and_5_out, statex, not_11_out, not_12_out, not_13_out);
  or or_1 (statex2, and_1_out, and_2_out, and_3_out);
  or or_2 (statey2, and_4_out, and_5_out);
endmodule

module \状态存储器  (
  input  in_1,
  input  in_2,
  input  clk,
  input  in_4,
  output out_5,
  output out_6
);

  wire multiplexer_1_out, multiplexer_2_out;

  Multiplexer multiplexer_1 (.in0(in_1), .in1(1'b1), .out(multiplexer_1_out), .sel(in_4));  // open: en
  Register #(.width(1)) register_1 (.D(multiplexer_1_out), .Q(out_5), .clk(clk));  // open: en, clr
  Multiplexer multiplexer_2 (.in0(in_2), .in1(1'b1), .out(multiplexer_2_out), .sel(in_4));  // open: en
  Register #(.width(1)) register_2 (.D(multiplexer_2_out), .Q(out_6), .clk(clk));  // open: en, clr
endmodule

module fsm (
  input  reset,
  input  [1:0] in,
  output out
);

  wire clock_1_out, \次态逻辑_1_statex2 , \次态逻辑_1_statey2 , \状态存储器_1_out_5 , \状态存储器_1_out_6 ;

  Clock clock_1 (.out(clock_1_out));
  \次态逻辑  \u_次态逻辑_1  (
    .statex(\状态存储器_1_out_5 ), .statey(\状态存储器_1_out_6 ), .in1(in[1]), .in2(in[0]), .clr(1'b0),
    .statex2(\次态逻辑_1_statex2 ), .statey2(\次态逻辑_1_statey2 ));
  \状态存储器  \u_状态存储器_1  (
    .in_1(\次态逻辑_1_statex2 ), .in_2(\次态逻辑_1_statey2 ), .clk(clock_1_out), .in_4(reset),
    .out_5(\状态存储器_1_out_5 ), .out_6(\状态存储器_1_out_6 ));
  \输出函数  \u_输出函数_1  (.in2(in[0]), .statex(\状态存储器_1_out_5 ), .statey(\状态存储器_1_out_6 ), .out(out));

  // Notes on the sheet:
  //   状态转换
  //   状态存储
  //   输出逻辑
endmodule
