// Logisim project ftoi.circ as structural Verilog: 4 circuits, main circuit ftoi
module ftoi (
  input  [15:0] in_1,
  output [31:0] out_2
);

  \输出函数  \u_输出函数_1  (.in_1(in_1), .out_2(out_2));
endmodule

module \输入函数  (
  input  [15:0] in_1,
  output sign,
  output [4:0] E,
  output flag,
  output [9:0] out_5
);

  wire flag0, subtractor_1_bout;

  // Probe on 5'b01111
  Subtractor #(.width(5)) subtractor_1 (.a(in_1[14:10]), .b(5'b01111), .out(E), .bout(subtractor_1_bout));  // open: bin
  or or_1 (flag, subtractor_1_bout, flag0);
  // Probe on in_1[14:10]
  Comparator #(.width(5)) comparator_1 (.a(in_1[14:10]), .b({5{1'b1}}), .eq(flag0));  // open: gt, lt
  // Probe on {5{1'b1}}

  assign out_5 = in_1[9:0];
  assign sign = in_1[15];

  // Other names for the same wires on the sheet: frac[9:0] = in_1[9:0]; ex[4:0] = in_1[14:10]

  // Notes on the sheet:
  //   减操作
endmodule

module \计算函数  (
  input  [15:0] E,
  output out_2,
  output [31:0] out_3,
  output out_4
);

  wire [4:0] E_t;
  wire [9:0] frac;
  wire [31:0] bit_extender_1_out, shifter_1_out;

  // Probe on E_t
  assign bit_extender_1_out = {{21{1'b0}}, {1'b1, frac}};  // Bit_Extender bit_extender_1
  \输入函数  \u_输入函数_1  (.in_1(E), .sign(out_2), .E(E_t), .flag(out_4), .out_5(frac));
  Shifter #(.width(32)) shifter_1 (.in(bit_extender_1_out), .\dist (E_t), .out(shifter_1_out));
  Shifter #(.width(32), .shift("lr")) shifter_2 (.in(shifter_1_out), .\dist (5'b01010), .out(out_3));
  // Probe on {1'b1, frac}

  // Other names for the same wires on the sheet: flag = out_4

  // Notes on the sheet:
  //   移位运算
  //   sign
  //   frac
  //   输入函数
endmodule

module \输出函数  (
  input  [15:0] in_1,
  output [31:0] out_2
);

  wire brac, sign;
  wire [31:0] demultiplexer_1_out0, demultiplexer_1_out1, multiplexer_1_out, negator_1_out, \计算函数_1_out_3 ;

  \计算函数  \u_计算函数_1  (.E(in_1), .out_2(sign), .out_3(\计算函数_1_out_3 ), .out_4(brac));
  Demultiplexer #(.width(32)) demultiplexer_1 (
    .out0(demultiplexer_1_out0), .out1(demultiplexer_1_out1), .in(\计算函数_1_out_3 ), .sel(sign));  // open: en
  Negator #(.width(32)) negator_1 (.in(demultiplexer_1_out1), .out(negator_1_out));
  Multiplexer #(.width(32)) multiplexer_1 (
    .in0(demultiplexer_1_out0), .in1(negator_1_out), .out(multiplexer_1_out), .sel(sign));  // open: en
  // Probe on \计算函数_1_out_3 
  Multiplexer #(.width(32)) multiplexer_2 (
    .in0(multiplexer_1_out), .in1({32{1'b0}}), .out(out_2), .sel(brac));  // open: en
endmodule
