// Logisim project navigation.circ as structural Verilog: 3 circuits, main circuit main
module main (
  input  a1,
  input  a2,
  input  a3,
  input  d1,
  input  d2,
  output a12,
  output a22,
  output a32,
  output arr,
  output h
);

  wire and_1_out, and_2_out, and_3_out, and_4_out, and_5_out, and_6_out, and_7_out, and_8_out, and_9_out,
       and_10_out, and_11_out, and_12_out, and_13_out, and_14_out, and_15_out, and_16_out, and_17_out,
       and_18_out, and_19_out, and_20_out, and_21_out, and_22_out, and_23_out, not_1_out, not_2_out,
       not_3_out, not_4_out, not_5_out, not_6_out, not_7_out, not_8_out, not_9_out, not_10_out, not_11_out,
       not_12_out, not_13_out, not_14_out, not_15_out, not_16_out, not_17_out, not_18_out, not_19_out,
       not_20_out, not_21_out, not_22_out, not_23_out, not_24_out, not_25_out, not_26_out, not_27_out,
       not_28_out, not_29_out, not_30_out, not_31_out, not_32_out, not_33_out, not_34_out, not_35_out,
       not_36_out, not_37_out, not_38_out;

  not not_1 (not_1_out, a1);
  not not_2 (not_2_out, d1);
  not not_3 (not_3_out, d2);
  not not_4 (not_4_out, a2);
  not not_5 (not_5_out, d1);
  not not_6 (not_6_out, a3);
  not not_7 (not_7_out, a2);
  not not_8 (not_8_out, a2);
  not not_9 (not_9_out, d1);
  not not_10 (not_10_out, a1);
  not not_11 (not_11_out, d2);
  not not_12 (not_12_out, a1);
  not not_13 (not_13_out, d1);
  not not_14 (not_14_out, a3);
  not not_15 (not_15_out, a2);
  not not_16 (not_16_out, d1);
  not not_17 (not_17_out, d2);
  not not_18 (not_18_out, a2);
  not not_19 (not_19_out, a1);
  not not_20 (not_20_out, a2);
  not not_21 (not_21_out, a3);
  not not_22 (not_22_out, a1);
  not not_23 (not_23_out, d1);
  not not_24 (not_24_out, d2);
  not not_25 (not_25_out, a3);
  not not_26 (not_26_out, a2);
  not not_27 (not_27_out, d1);
  not not_28 (not_28_out, a3);
  not not_29 (not_29_out, a3);
  not not_30 (not_30_out, a2);
  not not_31 (not_31_out, a1);
  not not_32 (not_32_out, d1);
  not not_33 (not_33_out, a1);
  not not_34 (not_34_out, d2);
  not not_35 (not_35_out, a2);
  not not_36 (not_36_out, d1);
  not not_37 (not_37_out, d2);
  not not_38 (not_38_out, a3);
  and and_1 (and_1_out, not_1_out, a3, not_2_out, not_3_out);
  and and_2 (and_2_out, a1, not_4_out, not_5_out);
  and and_3 (and_3_out, a1, not_6_out);
  and and_4 (and_4_out, a1, not_7_out, d2);
  and and_5 (and_5_out, not_8_out, a3, not_9_out, d2);
  and and_6 (and_6_out, not_10_out, a2, not_11_out);
  and and_7 (and_7_out, not_12_out, a2, a3, not_13_out);
  and and_8 (and_8_out, a1, not_14_out);
  and and_9 (and_9_out, not_15_out, not_16_out, not_17_out);
  and and_10 (and_10_out, not_18_out, a3, d2);
  and and_11 (and_11_out, not_19_out, a2);
  and and_12 (and_12_out, a1, not_20_out);
  and and_13 (and_13_out, a1, not_21_out);
  and and_14 (and_14_out, not_22_out, a2, not_23_out, not_24_out);
  and and_15 (and_15_out, a1, not_25_out);
  and and_16 (and_16_out, a1, not_26_out, not_27_out, d2);
  and and_17 (and_17_out, not_28_out, d2);
  and and_18 (and_18_out, not_29_out, d1);
  and and_19 (and_19_out, not_30_out, d1, d2);
  and and_20 (and_20_out, not_31_out, a2, not_32_out, d2);
  and and_21 (and_21_out, not_33_out, a2, d1, not_34_out);
  and and_22 (and_22_out, a1, not_35_out, not_36_out, not_37_out);
  and and_23 (and_23_out, a1, not_38_out);
  or or_1 (a12, and_1_out, and_2_out, and_3_out, and_4_out);
  or or_2 (a22, and_5_out, and_6_out, and_7_out, and_8_out);
  or or_3 (a32, and_9_out, and_10_out, and_11_out, and_12_out, and_13_out);
  or or_4 (arr, and_14_out, and_15_out, and_16_out);
  or or_5 (h, and_17_out, and_18_out, and_19_out, and_20_out, and_21_out, and_22_out, and_23_out);
endmodule

module \inout  (
  input  [1:0] dir,
  input  in_2,
  input  clk,
  input  reset,
  output arrive,
  output hit,
  output out_7
);

  wire clock_1_out, counter_1_carry, counter_2_carry, counter_3_carry, main_1_h, multiplexer_1_out,
       multiplexer_2_out, register_2_q, register_3_q;
  wire [2:0] new_state, register_1_q;

  // Probe on new_state
  // Probe on register_1_q
  Register #(.width(3)) register_1 (.D(new_state), .Q(register_1_q), .clk(clk), .clr(reset));  // open: en
  main main_1 (
    .a1(register_1_q[2]), .a2(register_1_q[1]), .a3(register_1_q[0]), .d1(multiplexer_1_out),
    .d2(multiplexer_2_out), .a12(new_state[2]), .a22(new_state[1]), .a32(new_state[0]), .arr(arrive),
    .h(main_1_h));
  Register #(.width(1)) register_2 (.D(dir[1]), .Q(register_2_q), .clk(clk));  // open: en, clr
  Register #(.width(1)) register_3 (.D(dir[0]), .Q(register_3_q), .clk(clk));  // open: en, clr
  Multiplexer multiplexer_1 (
    .in0(1'b1), .in1(register_2_q), .out(multiplexer_1_out), .sel(counter_1_carry));  // open: en
  Counter #(.width(1), .max('h1), .ongoal("stay")) counter_1 (
    .count(1'b1), .carry(counter_1_carry), .clk(clk), .clr(reset));  // open: load, D, Q
  Multiplexer multiplexer_2 (
    .in0(1'b1), .in1(register_3_q), .out(multiplexer_2_out), .sel(counter_2_carry));  // open: en
  Counter #(.width(1), .max('h1), .ongoal("stay")) counter_2 (
    .count(1'b1), .carry(counter_2_carry), .clk(clk), .clr(reset));  // open: load, D, Q
  Multiplexer multiplexer_3 (.in0(1'b0), .in1(main_1_h), .out(hit), .sel(counter_3_carry));  // open: en
  Counter #(.width(1), .max('h1), .ongoal("stay")) counter_3 (
    .count(1'b1), .carry(counter_3_carry), .clk(clk), .clr(reset));  // open: load, D, Q
  Clock clock_1 (.out(clock_1_out));
  Register #(.width(1)) register_4 (.D(in_2), .Q(out_7), .clk(clock_1_out));  // open: en, clr
endmodule

module navigation (
  input  [1:0] in_1,
  input  in_2,
  input  in_3,
  output out_4,
  output out_5
);

  \inout  inout_1 (.dir(in_1), .in_2(in_2), .clk(in_3), .arrive(out_4), .hit(out_5));  // open: reset, out_7
endmodule
