// Logisim project CPU单周期.circ as structural Verilog
module main (
  input  reset,
  output [31:0] out_2,
  output out_3,
  output [4:0] out_4,
  output [31:0] out_5,
  output out_6,
  output [4:0] out_7,
  output [31:0] out_8
);

  wire ALUsrc, Beq, beq_t, clk, MemR, Memtoreg, or_1_out, Oriop, Regdst, zero;
  wire [2:0] ALU_2_0;
  wire [31:0] ALUresult, data_in_rs, data_rt, \ext_位扩展_1_out_2 , \ext_位扩展_1_out_3 , immdata,
       multiplexer_1_out, multiplexer_3_out, \pc_程序计数器_1_out_4 , PCextern, PCplus, shifter_1_out, Wdata2;

  Clock clock_1 (.out(clk));
  Multiplexer #(.width(32)) multiplexer_1 (
    .in0(PCplus), .in1(PCextern), .out(multiplexer_1_out), .sel(beq_t));  // open: en
  // Probe on multiplexer_1_out
  // Probe on \pc_程序计数器_1_out_4 
  \PC_程序计数器  \pc_程序计数器_1  (.in_3(multiplexer_1_out), .out_4(\pc_程序计数器_1_out_4 ), .in_2(clk), .in_1(reset));
  \IM_指令存储器  \im_指令存储器_1  (.in_1(\pc_程序计数器_1_out_4 ), .out_2(out_2));
  PCplus pcplus_1 (.in_1(\pc_程序计数器_1_out_4 ), .in_2(32'h4), .out_3(PCplus));
  // Probe on out_2[25:21]
  or or_1 (or_1_out, ALUsrc, Beq);
  \EXT_位扩展  \ext_位扩展_1  (.in_1(out_2[15:0]), .out_2(\ext_位扩展_1_out_2 ), .out_3(\ext_位扩展_1_out_3 ));
  \Control_控制器  \control_控制器_1  (
    .in_1(out_2[5:0]), .in_2(out_2[31:26]), .out_3(Regdst), .out_4(ALUsrc), .out_5(Memtoreg), .out_6(out_3),
    .out_7(out_6), .out_9(Beq), .out_10(Oriop), .out_11(ALU_2_0[0]), .out_12(ALU_2_0[1]), .out_8(MemR),
    .out_13(ALU_2_0[2]));
  \GRF_寄存器堆  \grf_寄存器堆_1  (
    .in_1(out_2[25:21]), .in_4(out_2[20:16]), .in_5(out_4), .in_7(out_5), .out_8(data_in_rs), .out_9(out_8),
    .clk(clk), .Regw(out_3), .reset(reset));
  Multiplexer #(.width(5)) multiplexer_2 (
    .in0(out_2[20:16]), .in1(out_2[15:11]), .out(out_4), .sel(Regdst));  // open: en
  Multiplexer #(.width(32)) multiplexer_3 (
    .in0(\ext_位扩展_1_out_2 ), .in1(\ext_位扩展_1_out_3 ), .out(multiplexer_3_out), .sel(or_1_out));  // open: en
  Multiplexer #(.width(32)) multiplexer_4 (
    .in0(multiplexer_3_out), .in1(\ext_位扩展_1_out_2 ), .out(immdata), .sel(Oriop));  // open: en
  // Probe on immdata
  // Probe on data_in_rs
  // Probe on out_8
  Multiplexer #(.width(32)) multiplexer_5 (.in0(out_8), .in1(immdata), .out(data_rt), .sel(ALUsrc));  // open: en
  Shifter #(.width(32)) shifter_1 (.in(immdata), .\dist (5'b00010), .out(shifter_1_out));
  Adder #(.width(32)) adder_1 (.a(shifter_1_out), .b(PCplus), .out(PCextern));  // open: cin, cout
  // Probe on PCextern
  // Probe on data_in_rs
  // Probe on data_rt
  \ALU_算术逻辑  \alu_算术逻辑_1  (
    .ALUop(ALU_2_0), .Zero(zero), .ALUresult({ALUresult[31:7], out_7, ALUresult[1:0]}), .in_2(data_in_rs),
    .in_3(data_rt));
  and and_1 (beq_t, zero, Beq);
  // Probe on {ALUresult[31:7], out_7, ALUresult[1:0]}
  // Probe on out_8
  \DM_数据存储器  \dm_数据存储器_1  (
    .in_6(out_8), .ADD(out_7), .out_7(Wdata2), .clk(clk), .MemW(out_6), .MemR(MemR), .clr(reset));
  // Probe on {ALUresult[31:7], out_7, ALUresult[1:0]}
  // Probe on Wdata2
  Multiplexer #(.width(32)) multiplexer_6 (
    .in0({ALUresult[31:7], out_7, ALUresult[1:0]}), .in1(Wdata2), .out(out_5), .sel(Memtoreg));  // open: en

  // Other names for the same wires on the sheet: clr = reset; data_in_rt[31:0] = out_8; Instr[31:0] = out_2;
  //   MemW = out_6; rd_rt[4:0] = out_4; RegW = out_3; Wdata[31:0] = out_5;
  //   Wdata1[31:0] = {ALUresult[31:7], out_7, ALUresult[1:0]}; ADD[4:0] = out_7; ALUresult[6:2] = out_7

  // Notes on the sheet:
  //   clk
  //   rs:21~25
  //   rt:16~20
  //   rd:11~15
  //   shamft:6~10
  //   fun:0~5
  //   PC
  //   imm:0~15
  //   PC
  //   +
  //   PCplus
  //   Instr
  //   here it is replaced by MemR
  //   here it is replaced by Beq and ALUsrc
  //   im||0^2
  //   b_im
  //   PCplus
  //   PCextern
endmodule

module \GRF_寄存器堆  (
  input  [4:0] in_1,
  input  reset,
  input  clk,
  input  [4:0] in_4,
  input  [4:0] in_5,
  input  Regw,
  input  [31:0] in_7,
  output [31:0] out_8,
  output [31:0] out_9
);

  wire clk1, clk2, clk3, clk4, clk5, clk6, clk7, clk8, clk9, clk10, clk11, clk12, clk13, clk14, clk15, clk16,
       clk17, clk18, clk19, clk20, clk21, clk22, clk23, clk24, clk25, clk26, clk27, clk28, clk29, clk30,
       clk31, clk32;
  wire [31:0] R1, R2, R3, R4, R5, R6, R7, R8, R9, R10, R11, R12, R13, R14, R15, R16, R17, R18, R19, R20, R21,
       R22, R23, R24, R25, R26, R27, R28, R29, R30, R31, R32, W1, W2, W3, W4, W5, W6, W7, W8, W9, W10, W11,
       W12, W13, W14, W15, W16, W17, W18, W19, W20, W21, W22, W23, W24, W25, W26, W27, W28, W29, W30, W31,
       W32;

  Register #(.width(32)) register_1 (.D(W1), .en(1'b0), .Q(R1), .clk(clk), .clr(reset));
  Register #(.width(32)) register_2 (.D(W2), .en(clk2), .Q(R2), .clk(clk), .clr(reset));
  Register #(.width(32)) register_3 (.D(W3), .en(clk3), .Q(R3), .clk(clk), .clr(reset));
  Register #(.width(32)) register_4 (.D(W4), .en(clk4), .Q(R4), .clk(clk), .clr(reset));
  Register #(.width(32)) register_5 (.D(W5), .en(clk5), .Q(R5), .clk(clk), .clr(reset));
  Register #(.width(32)) register_6 (.D(W6), .en(clk6), .Q(R6), .clk(clk), .clr(reset));
  Register #(.width(32)) register_7 (.D(W7), .en(clk7), .Q(R7), .clk(clk), .clr(reset));
  Register #(.width(32)) register_8 (.D(W8), .en(clk8), .Q(R8), .clk(clk), .clr(reset));
  Demultiplexer #(.select(5), .width(32)) demultiplexer_1 (
    .out0(W1), .out1(W2), .out2(W3), .out3(W4), .out4(W5), .out5(W6), .out6(W7), .out7(W8), .out8(W9),
    .out9(W10), .out10(W11), .out11(W12), .out12(W13), .out13(W14), .out14(W15), .out15(W16), .out16(W17),
    .out17(W18), .out18(W19), .out19(W20), .out20(W21), .out21(W22), .out22(W23), .out23(W24), .out24(W25),
    .out25(W26), .out26(W27), .out27(W28), .out28(W29), .out29(W30), .out30(W31), .out31(W32), .in(in_7),
    .sel(in_5));  // open: en
  Register #(.width(32)) register_9 (.D(W9), .en(clk9), .Q(R9), .clk(clk), .clr(reset));
  Register #(.width(32)) register_10 (.D(W10), .en(clk10), .Q(R10), .clk(clk), .clr(reset));
  Register #(.width(32)) register_11 (.D(W11), .en(clk11), .Q(R11), .clk(clk), .clr(reset));
  Register #(.width(32)) register_12 (.D(W12), .en(clk12), .Q(R12), .clk(clk), .clr(reset));
  Register #(.width(32)) register_13 (.D(W13), .en(clk13), .Q(R13), .clk(clk), .clr(reset));
  Register #(.width(32)) register_14 (.D(W14), .en(clk14), .Q(R14), .clk(clk), .clr(reset));
  Register #(.width(32)) register_15 (.D(W15), .en(clk15), .Q(R15), .clk(clk), .clr(reset));
  Register #(.width(32)) register_16 (.D(W16), .en(clk16), .Q(R16), .clk(clk), .clr(reset));
  Register #(.width(32)) register_17 (.D(W17), .en(clk17), .Q(R17), .clk(clk), .clr(reset));
  Register #(.width(32)) register_18 (.D(W18), .en(clk18), .Q(R18), .clk(clk), .clr(reset));
  Register #(.width(32)) register_19 (.D(W19), .en(clk19), .Q(R19), .clk(clk), .clr(reset));
  Register #(.width(32)) register_20 (.D(W20), .en(clk20), .Q(R20), .clk(clk), .clr(reset));
  Register #(.width(32)) register_21 (.D(W21), .en(clk21), .Q(R21), .clk(clk), .clr(reset));
  Register #(.width(32)) register_22 (.D(W22), .en(clk22), .Q(R22), .clk(clk), .clr(reset));
  Register #(.width(32)) register_23 (.D(W23), .en(clk23), .Q(R23), .clk(clk), .clr(reset));
  Register #(.width(32)) register_24 (.D(W24), .en(clk24), .Q(R24), .clk(clk), .clr(reset));
  Register #(.width(32)) register_25 (.D(W25), .en(clk25), .Q(R25), .clk(clk), .clr(reset));
  Register #(.width(32)) register_26 (.D(W26), .en(clk26), .Q(R26), .clk(clk), .clr(reset));
  Register #(.width(32)) register_27 (.D(W27), .en(clk27), .Q(R27), .clk(clk), .clr(reset));
  Register #(.width(32)) register_28 (.D(W28), .en(clk28), .Q(R28), .clk(clk), .clr(reset));
  Register #(.width(32)) register_29 (.D(W29), .en(clk29), .Q(R29), .clk(clk), .clr(reset));
  Register #(.width(32)) register_30 (.D(W30), .en(clk30), .Q(R30), .clk(clk), .clr(reset));
  Register #(.width(32)) register_31 (.D(W31), .en(clk31), .Q(R31), .clk(clk), .clr(reset));
  Register #(.width(32)) register_32 (.D(W32), .en(clk32), .Q(R32), .clk(clk), .clr(reset));
  // Probe on W9
  // Probe on W10
  Demultiplexer #(.select(5)) demultiplexer_2 (
    .out0(clk1), .out1(clk2), .out2(clk3), .out3(clk4), .out4(clk5), .out5(clk6), .out6(clk7), .out7(clk8),
    .out8(clk9), .out9(clk10), .out10(clk11), .out11(clk12), .out12(clk13), .out13(clk14), .out14(clk15),
    .out15(clk16), .out16(clk17), .out17(clk18), .out18(clk19), .out19(clk20), .out20(clk21), .out21(clk22),
    .out22(clk23), .out23(clk24), .out24(clk25), .out25(clk26), .out26(clk27), .out27(clk28), .out28(clk29),
    .out29(clk30), .out30(clk31), .out31(clk32), .in(Regw), .sel(in_5));  // open: en
  Multiplexer #(.select(5), .width(32)) multiplexer_1 (
    .in0({32{1'b0}}), .in1(R2), .in2(R3), .in3(R4), .in4(R5), .in5(R6), .in6(R7), .in7(R8), .in8(R9),
    .in9(R10), .in10(R11), .in11(R12), .in12(R13), .in13(R14), .in14(R15), .in15(R16), .in16(R17),
    .in17(R18), .in18(R19), .in19(R20), .in20(R21), .in21(R22), .in22(R23), .in23(R24), .in24(R25),
    .in25(R26), .in26(R27), .in27(R28), .in28(R29), .in29(R30), .in30(R31), .in31(R32), .out(out_8),
    .sel(in_1));  // open: en
  Multiplexer #(.select(5), .width(32)) multiplexer_2 (
    .in0({32{1'b0}}), .in1(R2), .in2(R3), .in3(R4), .in4(R5), .in5(R6), .in6(R7), .in7(R8), .in8(R9),
    .in9(R10), .in10(R11), .in11(R12), .in12(R13), .in13(R14), .in14(R15), .in15(R16), .in16(R17),
    .in17(R18), .in18(R19), .in19(R20), .in20(R21), .in21(R22), .in22(R23), .in23(R24), .in24(R25),
    .in25(R26), .in26(R27), .in27(R28), .in28(R29), .in29(R30), .in30(R31), .in31(R32), .out(out_9),
    .sel(in_4));  // open: en
endmodule

module \ALU_算术逻辑  (
  input  [2:0] ALUop,
  input  [31:0] in_2,
  input  [31:0] in_3,
  output Zero,
  output [31:0] ALUresult
);

  wire [31:0] add1, add2, AR, LR, lui, OR, or1, or2, SR, sub1, sub2;

  Demultiplexer #(.select(3), .width(32)) demultiplexer_1 (
    .out1(or1), .out2(add1), .out3(sub1), .in(in_2), .sel(ALUop));  // open: out0, out4, out5, out6, out7, en
  Demultiplexer #(.select(3), .width(32)) demultiplexer_2 (
    .out1(or2), .out2(add2), .out3(sub2), .out6(lui), .in(in_3), .sel(ALUop));  // open: out0, out4, out5, out7, en
  // Probe on or1
  Subtractor #(.width(32)) subtractor_1 (.a(sub1), .b(sub2), .out(SR));  // open: bin, bout
  assign OR = or1 | or2;  // OR_Gate or_1, 32 bits wide
  Adder #(.width(32)) adder_1 (.a(add1), .b(add2), .out(AR));  // open: cin, cout
  Shifter #(.width(32)) shifter_1 (.in(lui), .\dist (5'b10000), .out(LR));
  Comparator #(.width(32)) comparator_1 (.a(SR), .b({32{1'b0}}), .eq(Zero));  // open: gt, lt
  Multiplexer #(.select(3), .width(32)) multiplexer_1 (
    .in1(OR), .in2(AR), .in3(SR), .in6(LR), .out(ALUresult), .sel(ALUop));  // open: in0, in4, in5, in7, en

  // Notes on the sheet:
  //   RD1
  //   RD2
endmodule

module \DM_数据存储器  (
  input  MemW,
  input  clk,
  input  MemR,
  input  clr,
  input  [4:0] ADD,
  input  [31:0] in_6,
  output [31:0] out_7
);

  RAM #(.addrWidth(5), .dataWidth(32), .bus("separate")) ram_1 (
    .addr(ADD), .din(in_6), .data(out_7), .str(MemW), .clk(clk), .ld(MemR), .clr(clr));  // open: sel

  // Notes on the sheet:
  //   Wdata
  //   Rdata
endmodule

module \EXT_位扩展  (
  input  [15:0] in_1,
  output [31:0] out_2,
  output [31:0] out_3
);

  assign out_2 = {{16{1'b0}}, in_1};  // Bit_Extender bit_extender_1
  assign out_3 = {{16{in_1[15]}}, in_1};  // Bit_Extender bit_extender_2
endmodule

module \Control_控制器  (
  input  [5:0] in_1,
  input  [5:0] in_2,
  output out_3,
  output out_4,
  output out_5,
  output out_6,
  output out_7,
  output out_8,
  output out_9,
  output out_10,
  output out_11,
  output out_12,
  output out_13
);

  wire and_logic_1_out_3, and_logic_1_out_4, and_logic_1_out_5, and_logic_1_out_6, and_logic_1_out_7,
       and_logic_1_out_8, and_logic_1_out_9;

  AND_logic and_logic_1 (
    .in_1(in_1), .op(in_2), .out_3(and_logic_1_out_3), .out_4(and_logic_1_out_4), .out_5(and_logic_1_out_5),
    .out_6(and_logic_1_out_6), .out_7(and_logic_1_out_7), .out_8(and_logic_1_out_8), .out_9(and_logic_1_out_9));
  OR_logic or_logic_1 (
    .addu(and_logic_1_out_3), .subu(and_logic_1_out_4), .beq(and_logic_1_out_5), .lui(and_logic_1_out_6),
    .lw(and_logic_1_out_7), .ori(and_logic_1_out_8), .sw(and_logic_1_out_9), .RegDst(out_3), .ALUSrc(out_4),
    .MemtoReg(out_5), .RegW(out_6), .Memw(out_7), .ZeroOp(out_10), .ALU0(out_11), .ALU1(out_12),
    .ALU2(out_13), .beq_2(out_9), .MemR(out_8));
endmodule

module \PC_程序计数器  (
  input  in_1,
  input  in_2,
  input  [31:0] in_3,
  output [31:0] out_4
);

  Register #(.width(32)) register_1 (.D(in_3), .Q(out_4), .clk(in_2), .clr(in_1));  // open: en

  // Notes on the sheet:
  //   a register
endmodule

module \IM_指令存储器  (
  input  [31:0] in_1,
  output [31:0] out_2
);

  ROM #(.addrWidth(5), .dataWidth(32)) rom_1 (.addr(in_1[6:2]), .data(out_2));  // open: sel

  // Notes on the sheet:
  //   PC
  //   contents of rom_1 (hex, n*v repeats v):
  //   34210064 224021 210821
  //   instr
endmodule

module PCplus (
  input  [31:0] in_1,
  input  [31:0] in_2,
  output [31:0] out_3
);

  Adder #(.width(32)) adder_1 (.a(in_1), .b(in_2), .out(out_3));  // open: cin, cout
endmodule

module AND_logic (
  input  [5:0] in_1,
  input  [5:0] op,
  output out_3,
  output out_4,
  output out_5,
  output out_6,
  output out_7,
  output out_8,
  output out_9
);

  wire not_1_out, not_2_out, not_3_out, not_4_out, not_5_out, not_6_out, not_7_out, not_8_out, not_9_out,
       not_10_out, not_11_out, not_12_out, R_out;

  not not_1 (not_1_out, op[5]);
  not not_2 (not_2_out, op[4]);
  not not_3 (not_3_out, op[3]);
  not not_4 (not_4_out, op[2]);
  not not_5 (not_5_out, op[1]);
  not not_6 (not_6_out, op[0]);
  and R (R_out, not_6_out, not_5_out, not_4_out, not_3_out, not_2_out, not_1_out);
  and beq (out_5, not_6_out, not_5_out, op[2], not_3_out, not_2_out, not_1_out);
  and lui (out_6, op[0], op[1], op[2], op[3], not_2_out, not_1_out);
  and lw (out_7, op[0], op[1], not_4_out, not_3_out, not_2_out, op[5]);
  and ori (out_8, op[0], not_5_out, op[2], op[3], not_2_out, not_1_out);
  and sw (out_9, op[0], op[1], not_4_out, op[3], not_2_out, op[5]);
  not not_7 (not_7_out, in_1[5]);
  not not_8 (not_8_out, in_1[4]);
  not not_9 (not_9_out, in_1[3]);
  not not_10 (not_10_out, in_1[2]);
  not not_11 (not_11_out, in_1[1]);
  not not_12 (not_12_out, in_1[0]);
  and addu (out_3, in_1[0], not_11_out, not_10_out, not_8_out, in_1[5], R_out);
  and subu (out_4, in_1[0], in_1[1], not_9_out, not_8_out, in_1[5], R_out);
endmodule

module OR_logic (
  input  addu,
  input  subu,
  input  beq,
  input  lui,
  input  lw,
  input  ori,
  input  sw,
  output RegDst,
  output ALUSrc,
  output MemtoReg,
  output RegW,
  output Memw,
  output MemR,
  output beq_2,
  output ZeroOp,
  output ALU0,
  output ALU1,
  output ALU2
);

  or or_1 (RegDst, addu, subu);
  or or_2 (ALUSrc, lui, lw, ori, sw);
  buf or_3 (MemtoReg, lw);  // OR_Gate
  or or_4 (RegW, addu, subu, lui, lw, ori);
  buf or_5 (Memw, sw);  // OR_Gate
  buf or_6 (MemR, lw);  // OR_Gate
  buf or_7 (beq_2, beq);  // OR_Gate
  buf or_8 (ZeroOp, ori);  // OR_Gate
  or or_9 (ALU0, subu, beq, ori);
  or or_10 (ALU1, lw, addu, subu, beq, sw, lui);
  buf or_11 (ALU2, lui);  // OR_Gate
endmodule
