// Logisim project main.circ as structural Verilog: 4 circuits, main circuit main
module main (
  input  [2:0] in_1,
  output [3:0] out_2
);

  \计算端  \u_计算端_1  (.in_1(in_1), .out_2(out_2));
endmodule

module \输入端  (
  input  in_1,
  input  [2:0] in_2,
  output out_3
);

  wire counter_1_q;

  Counter #(.width(1), .max('h1), .ongoal("stay")) counter_1 (
    .load(1'b0), .count(1'b1), .Q(counter_1_q), .clk(in_1));  // open: D, carry, clr
  Counter #(.width(3), .max('h7), .ongoal("stay")) counter_2 (
    .load(1'b1), .D(in_2), .count(counter_1_q), .carry(out_3), .clk(in_1));  // open: Q, clr
  Register #(.width(1)) register_1 (.D(out_3), .clk(in_1));  // open: en, Q, clr
endmodule

module \计算端  (
  input  [2:0] in_1,
  output [3:0] out_2
);

  wire clock_1_out, counter_1_carry, not_1_out, not_2_out, register_1_q, register_4_q, xnor_1_out,
       \输入端_1_out_3 ;
  wire [3:0] adder_1_out, multiplexer_1_out, multiplexer_2_out, multiplexer_3_out, register_2_q, register_3_q;

  Clock clock_1 (.out(clock_1_out));
  Counter #(.width(1), .max('h1), .ongoal("stay")) counter_1 (
    .load(1'b0), .count(1'b1), .carry(counter_1_carry), .clk(clock_1_out));  // open: D, Q, clr
  Multiplexer #(.width(4)) multiplexer_1 (
    .in0(4'b0000), .in1(register_3_q), .out(multiplexer_1_out), .sel(counter_1_carry));  // open: en
  Multiplexer #(.width(4)) multiplexer_2 (
    .in0(4'b0001), .in1(adder_1_out), .out(multiplexer_2_out), .sel(register_1_q));  // open: en
  Register #(.width(1)) register_1 (.D(not_1_out), .Q(register_1_q), .clk(clock_1_out));  // open: en, clr
  \输入端  \u_输入端_1  (.in_1(clock_1_out), .in_2(in_1), .out_3(\输入端_1_out_3 ));
  Register #(.width(4)) register_2 (
    .D(multiplexer_1_out), .en(not_1_out), .Q(register_2_q), .clk(clock_1_out));  // open: clr
  Register #(.width(4)) register_3 (
    .D(multiplexer_2_out), .en(not_1_out), .Q(register_3_q), .clk(clock_1_out));  // open: clr
  not not_1 (not_1_out, \输入端_1_out_3 );
  Adder #(.width(4)) adder_1 (.a(register_2_q), .b(register_3_q), .out(adder_1_out));  // open: cin, cout
  Multiplexer #(.width(4)) multiplexer_3 (
    .in0(4'b0000), .in1(register_2_q), .out(multiplexer_3_out), .sel(\输入端_1_out_3 ));  // open: en
  xnor xnor_1 (xnor_1_out, 1'b1, \输入端_1_out_3 );
  Counter #(.width(4), .max('hf), .ongoal("load")) counter_2 (
    .load(1'b1), .D(multiplexer_3_out), .count(1'b0), .Q(out_2), .clk(register_4_q));  // open: carry, clr
  Register #(.width(1)) register_4 (.D(xnor_1_out), .Q(register_4_q), .clk(not_2_out));  // open: en, clr
  not not_2 (not_2_out, clock_1_out);
endmodule

module ceshi (
  input  [1:0] in_1,
  input  in_2,
  output [1:0] out_3
);

  wire clock_1_out;

  Clock clock_1 (.out(clock_1_out));
  Counter #(.width(2), .max('h3)) counter_1 (
    .load(clock_1_out), .D(in_1), .count(in_2), .Q(out_3), .clk(clock_1_out));  // open: carry, clr
endmodule
