// Logisim project main2.circ as structural Verilog: 6 circuits, main circuit 核心运算2
module \核心运算2  (
  input  [31:0] in_1,
  output [31:0] out_2
);

  wire \核心运算_1_out_2 ;
  wire [31:0] \核心运算_1_out_3 ;

  \核心运算  \u_核心运算_1  (.\输入 (in_1), .out_2(\核心运算_1_out_2 ), .out_3(\核心运算_1_out_3 ));
  Multiplexer #(.width(32)) multiplexer_1 (
    .in0({32{1'b0}}), .in1(\核心运算_1_out_3 ), .out(out_2), .sel(\核心运算_1_out_2 ));  // open: en

  // Notes on the sheet:
  //   取低位
  //   终止信号
endmodule

module \输入逻辑  (
  input  [31:0] in_1,
  output out_2,
  output out_3
);

  wire and_1_out, clock_1_out, comparator_1_eq, counter_1_q, not_1_out;
  wire [31:0] multiplexer_1_out, register_1_q, register_2_q, shifter_1_out;

  not not_1 (not_1_out, counter_1_q);
  Counter #(.width(1), .max('h1), .ongoal("stay")) counter_1 (
    .count(1'b1), .Q(counter_1_q), .clk(clock_1_out));  // open: load, D, carry, clr
  Multiplexer #(.width(32)) multiplexer_1 (
    .in0(register_1_q), .in1(in_1), .out(multiplexer_1_out), .sel(not_1_out));  // open: en
  Shifter #(.width(32), .shift("lr")) shifter_1 (.in(multiplexer_1_out), .\dist (5'b00001), .out(shifter_1_out));
  Register #(.width(32)) register_1 (.D(shifter_1_out), .Q(register_1_q), .clk(clock_1_out));  // open: en, clr
  Register #(.width(32)) register_2 (.D(multiplexer_1_out), .Q(register_2_q), .clk(clock_1_out));  // open: en, clr
  Comparator #(.width(32)) comparator_1 (.a(shifter_1_out), .b({32{1'b0}}), .eq(comparator_1_eq));  // open: gt, lt
  BitSelector #(.width(32)) bitselector_1 (.in(register_2_q), .out(out_2), .sel({5{1'b0}}));
  Clock clock_1 (.out(clock_1_out));
  and and_1 (and_1_out, out_2, comparator_1_eq);
  Counter #(.width(1), .max('h1)) counter_2 (.count(1'b1), .carry(out_3), .clk(and_1_out));  // open: load, D, Q, clr
  // Probe on register_1_q
  // Probe on shifter_1_out

  // Notes on the sheet:
  //   32位二进制数
  //   右移移位
  //   挑出末位
endmodule

module \计算逻辑  (
  output [31:0] out_1,
  output [31:0] out_2,
  output [31:0] out_3,
  output [31:0] out_4
);

  wire clock_1_out, counter_1_carry, multiplexer_5_out, register_1_q, register_2_q, \初始化_1_out_1 ,
       \初始化_2_out_1 , \初始化_3_out_1 , \初始化_4_out_1 ;
  wire [31:0] adder_1_out, adder_2_out, adder_3_out, adder_4_out, multiplier_1_out, multiplier_2_out,
       multiplier_3_out, multiplier_4_out, multiplier_5_out, multiplier_6_out, multiplier_7_out,
       multiplier_8_out, na11, na12, na21, na22;

  \初始化  \u_初始化_1  (.out_1(\初始化_1_out_1 ));
  \初始化  \u_初始化_2  (.out_1(\初始化_2_out_1 ));
  \初始化  \u_初始化_3  (.out_1(\初始化_3_out_1 ));
  \初始化  \u_初始化_4  (.out_1(\初始化_4_out_1 ));
  Multiplexer #(.width(32)) multiplexer_1 (.in0(32'h1), .in1(na11), .out(out_1), .sel(\初始化_1_out_1 ));  // open: en
  Multiplexer #(.width(32)) multiplexer_2 (.in0(32'h1), .in1(na12), .out(out_2), .sel(\初始化_2_out_1 ));  // open: en
  Multiplexer #(.width(32)) multiplexer_3 (.in0(32'h1), .in1(na21), .out(out_3), .sel(\初始化_3_out_1 ));  // open: en
  Multiplexer #(.width(32)) multiplexer_4 (.in0({32{1'b0}}), .in1(na22), .out(out_4), .sel(\初始化_4_out_1 ));  // open: en
  Clock clock_1 (.out(clock_1_out));
  Multiplier #(.width(32)) multiplier_1 (.a(out_1), .b(out_1), .out(multiplier_1_out));  // open: cin, cout
  Multiplier #(.width(32)) multiplier_2 (.a(out_2), .b(out_3), .out(multiplier_2_out));  // open: cin, cout
  Multiplier #(.width(32)) multiplier_3 (.a(out_1), .b(out_2), .out(multiplier_3_out));  // open: cin, cout
  Multiplier #(.width(32)) multiplier_4 (.a(out_2), .b(out_4), .out(multiplier_4_out));  // open: cin, cout
  Multiplier #(.width(32)) multiplier_5 (.a(out_3), .b(out_1), .out(multiplier_5_out));  // open: cin, cout
  Multiplier #(.width(32)) multiplier_6 (.a(out_4), .b(out_3), .out(multiplier_6_out));  // open: cin, cout
  Multiplier #(.width(32)) multiplier_7 (.a(out_3), .b(out_2), .out(multiplier_7_out));  // open: cin, cout
  Multiplier #(.width(32)) multiplier_8 (.a(out_4), .b(out_4), .out(multiplier_8_out));  // open: cin, cout
  Register #(.width(1)) register_1 (.D(register_2_q), .Q(register_1_q), .clk(clock_1_out));  // open: en, clr
  Register #(.width(1)) register_2 (.D(clock_1_out), .Q(register_2_q), .clk(clock_1_out));  // open: en, clr
  Adder #(.width(32)) adder_1 (.a(multiplier_1_out), .b(multiplier_2_out), .out(adder_1_out));  // open: cin, cout
  Adder #(.width(32)) adder_2 (.a(multiplier_3_out), .b(multiplier_4_out), .out(adder_2_out));  // open: cin, cout
  Adder #(.width(32)) adder_3 (.a(multiplier_5_out), .b(multiplier_6_out), .out(adder_3_out));  // open: cin, cout
  Adder #(.width(32)) adder_4 (.a(multiplier_7_out), .b(multiplier_8_out), .out(adder_4_out));  // open: cin, cout
  Multiplexer multiplexer_5 (
    .in0(1'b0), .in1(clock_1_out), .out(multiplexer_5_out), .sel(counter_1_carry));  // open: en
  Counter #(.width(1), .max('h1), .ongoal("stay")) counter_1 (
    .count(1'b1), .carry(counter_1_carry), .clk(register_1_q));  // open: load, D, Q, clr
  Register #(.width(32)) register_3 (.D(adder_1_out), .Q(na11), .clk(multiplexer_5_out));  // open: en, clr
  Register #(.width(32)) register_4 (.D(adder_2_out), .Q(na12), .clk(multiplexer_5_out));  // open: en, clr
  Register #(.width(32)) register_5 (.D(adder_3_out), .Q(na21), .clk(multiplexer_5_out));  // open: en, clr
  Register #(.width(32)) register_6 (.D(adder_4_out), .Q(na22), .clk(multiplexer_5_out));  // open: en, clr

  // Other names for the same wires on the sheet: a11[31:0] = out_1; a12[31:0] = out_2; a21[31:0] = out_3;
  //   a22[31:0] = out_4

  // Notes on the sheet:
  //   a12
  //   a21
  //   a22
  //   初始矩阵为1110
  //   a11
  //   矩阵转换和输出
endmodule

module \初始化  (
  output out_1
);

  wire clock_1_out, register_1_q, register_2_q;

  Clock clock_1 (.out(clock_1_out));
  Register #(.width(1)) register_1 (.D(clock_1_out), .Q(register_1_q), .clk(clock_1_out));  // open: en, clr
  Register #(.width(1)) register_2 (.D(register_1_q), .Q(register_2_q), .clk(clock_1_out));  // open: en, clr
  Counter #(.width(1), .max('h1), .ongoal("stay")) counter_1 (
    .count(1'b1), .carry(out_1), .clk(register_2_q));  // open: load, D, Q, clr
endmodule

module \核心运算  (
  input  [31:0] \输入 ,
  output out_2,
  output [31:0] out_3
);

  wire clock_1_out, counter_1_carry, \输入逻辑_1_out_2 ;
  wire [31:0] a1, a2, a3, a4, multiplexer_1_out, multiplexer_2_out, register_1_q, register_2_q, s1, s2, s3,
       s4, sn, \计算逻辑_1_out_1 , \计算逻辑_1_out_2 , \计算逻辑_1_out_3 , \计算逻辑_1_out_4 ;

  \计算逻辑  \u_计算逻辑_1  (.out_1(\计算逻辑_1_out_1 ), .out_2(\计算逻辑_1_out_2 ), .out_3(\计算逻辑_1_out_3 ), .out_4(\计算逻辑_1_out_4 ));
  \输入逻辑  \u_输入逻辑_1  (.in_1(\输入 ), .out_2(\输入逻辑_1_out_2 ), .out_3(out_2));
  Multiplexer #(.width(32)) multiplexer_1 (
    .in0(32'h1), .in1(sn), .out(multiplexer_1_out), .sel(counter_1_carry));  // open: en
  Counter #(.width(1), .max('h1), .ongoal("stay")) counter_1 (
    .count(1'b1), .carry(counter_1_carry), .clk(clock_1_out));  // open: load, D, Q, clr
  Multiplexer #(.width(32)) multiplexer_2 (
    .in0({32{1'b0}}), .in1(out_3), .out(multiplexer_2_out), .sel(counter_1_carry));  // open: en
  Clock clock_1 (.out(clock_1_out));
  Register #(.width(32)) register_1 (.D(multiplexer_1_out), .Q(register_1_q), .clk(clock_1_out));  // open: en, clr
  Register #(.width(32)) register_2 (.D(multiplexer_2_out), .Q(register_2_q), .clk(clock_1_out));  // open: en, clr
  Multiplexer #(.width(32)) multiplexer_3 (
    .in0(32'h1), .in1(\计算逻辑_1_out_1 ), .out(a1), .sel(\输入逻辑_1_out_2 ));  // open: en
  Multiplexer #(.width(32)) multiplexer_4 (
    .in0({32{1'b0}}), .in1(\计算逻辑_1_out_2 ), .out(a2), .sel(\输入逻辑_1_out_2 ));  // open: en
  Multiplier #(.width(32)) multiplier_1 (.a(a1), .b(register_1_q), .out(s1));  // open: cin, cout
  Multiplier #(.width(32)) multiplier_2 (.a(a3), .b(register_1_q), .out(s3));  // open: cin, cout
  Multiplier #(.width(32)) multiplier_3 (.a(a2), .b(register_2_q), .out(s2));  // open: cin, cout
  Multiplier #(.width(32)) multiplier_4 (.a(a4), .b(register_2_q), .out(s4));  // open: cin, cout
  Multiplexer #(.width(32)) multiplexer_5 (
    .in0({32{1'b0}}), .in1(\计算逻辑_1_out_3 ), .out(a3), .sel(\输入逻辑_1_out_2 ));  // open: en
  Adder #(.width(32)) adder_1 (.a(s1), .b(s2), .out(sn));  // open: cin, cout
  Adder #(.width(32)) adder_2 (.a(s3), .b(s4), .out(out_3));  // open: cin, cout
  Multiplexer #(.width(32)) multiplexer_6 (
    .in0(32'h1), .in1(\计算逻辑_1_out_4 ), .out(a4), .sel(\输入逻辑_1_out_2 ));  // open: en

  // Other names for the same wires on the sheet: sn_1[31:0] = out_3

  // Notes on the sheet:
  //   f(n)
  //   f(n-1)
  //   取出最低值
  //   f(n0)
endmodule

module main (
  input  [31:0] in_1,
  output [31:0] out_2
);

  \核心运算2  \u_核心运算2_1  (.in_1(in_1), .out_2(out_2));
endmodule
