// Logisim project mod5.circ as structural Verilog
module mod5 (
  input  in,
  output out_2,
  output s1,
  output s2,
  output s3,
  output s4
);

  wire and_1_out, and_2_out, and_5_out, and_6_out, clock_1_out, not_1_out, not_2_out, not_3_out, not_4_out,
       not_5_out, not_6_out, not_7_out, register_1_q, register_2_q;

  not not_1 (not_1_out, in);
  not not_2 (not_2_out, register_1_q);
  not not_3 (not_3_out, register_2_q);
  not not_4 (not_4_out, register_1_q);
  not not_5 (not_5_out, register_2_q);
  and and_1 (and_1_out, in, register_2_q);
  and and_2 (and_2_out, in, register_1_q);
  not not_6 (not_6_out, in);
  not not_7 (not_7_out, in);
  and and_3 (s1, not_1_out, not_2_out, not_3_out);
  and and_4 (s2, in, not_4_out, not_5_out);
  or or_1 (s3, and_1_out, and_2_out);
  and and_5 (and_5_out, not_6_out, register_2_q);
  and and_6 (and_6_out, not_7_out, register_1_q);
  or or_2 (s4, and_5_out, and_6_out);
  Clock clock_1 (.out(clock_1_out));
  Register #(.width(1)) register_1 (.D(s2), .Q(register_1_q), .clk(clock_1_out));  // open: en, clr
  Register #(.width(1)) register_2 (.D(s3), .Q(register_2_q), .clk(clock_1_out));  // open: en, clr

  assign out_2 = 1'b0;
endmodule
