// Logisim project mod5cnm.circ as structural Verilog: 2 circuits, main circuit main
module main (
  output out_1,
  output out_2,
  output out_3,
  output out_4,
  output out_5,
  output out_6,
  output out_7
);

  wire clock_1_out;
  wire [3:0] counter_1_q;

  Counter #(.width(4), .max('hf)) counter_1 (
    .Q(counter_1_q), .carry(out_6), .clk(clock_1_out));  // open: load, D, count, clr
  Clock clock_1 (.out(clock_1_out));
  ROM #(.addrWidth(4), .dataWidth(1)) rom_1 (.addr(counter_1_q), .data(out_1));  // open: sel
  mod5 mod5_1 (.in_1(out_1), .out_2(out_2), .out_3(out_3), .out_4(out_4), .out_5(out_5), .out_6(out_7));

  // Notes on the sheet:
  //   contents of rom_1 (hex, n*v repeats v):
  //   0 0 1 0 0 1 0 0 1
endmodule

module mod5 (
  input  in_1,
  output out_2,
  output out_3,
  output out_4,
  output out_5,
  output out_6
);

  wire clock_1_out, not_1_out, not_2_out, register_3_q;

  Register #(.width(1)) register_1 ();  // open: D, en, Q, clk, clr
  Register #(.width(1)) register_2 ();  // open: D, en, Q, clk, clr
  Register #(.width(1)) register_3 (.D(in_1), .Q(register_3_q), .clk(clock_1_out));  // open: en, clr
  Clock clock_1 (.out(clock_1_out));
  not not_1 (not_1_out, in_1);
  not not_2 (not_2_out, register_3_q);
  and and_1 (out_3, not_2_out, not_1_out);
  and and_2 (out_4, not_2_out, in_1);
  and and_3 (out_5, register_3_q, in_1);
  and and_4 (out_6, register_3_q, not_1_out);

  assign out_2 = 1'b0;
endmodule
